# Fritzing sketch transmitter (saved by Fritzing 0.9.3b)
breadboards: 2

parts:
  X2 = X113647 Stepper Driver Board [part_number=X113647 package=board]
  R1 = Resistor [tolerance=±5% resistance=10k package="0805 [SMD]"]
  MOTOR4 = 28BYJ-48 Stepper Motor
  Part1 = Arduino Uno (Rev3)
  S2 = Pushbutton [package="[THT]"]
  HC-SR04_Sensor_3 = HC-SR04 Ultrasonic Distance Sensor

nets:
  N1: X2.IN1, Part1.D8
  N2: X2.IN2, Part1.D10_PWM/SS
  N3: X2.IN3, Part1.D9_PWM
  N4: X2.IN4, Part1.D11_PWM/MOSI
  GND: X2.GND, R1.Pin_1, Part1.GND, HC-SR04_Sensor_3.GND
  5V: X2.+V, Part1.5V, S2.Pin_3, S2.Pin_4, HC-SR04_Sensor_3.VCC
  N5: X2.BLUE, MOTOR4.BLUE
  N6: X2.PINK, MOTOR4.PINK
  N7: X2.YELLOW, MOTOR4.YELLOW
  N8: X2.ORANGE, MOTOR4.ORANGE
  N9: X2.RED, MOTOR4.RED
  N10: R1.Pin_0, Part1.D4, S2.Pin_1, S2.Pin_2
  N11: Part1.D2, HC-SR04_Sensor_3.TRIG
  N12: Part1.D3_PWM, HC-SR04_Sensor_3.ECHO

custom parts:
  X113647 Stepper Driver Board: A common stepper motor driver board based on ULN2003APG darlington array
  28BYJ-48 Stepper Motor: 28BYJ-48 gear-reduction stepper motor (small)
  HC-SR04 Ultrasonic Distance Sensor: The HC-SR04 is an ultrasonic distance sensor. It is capable of providing measurement for ranges of 2cm to 400cm. The module operates at 5V.
